# Fritzing sketch letterbox_board_pcb (saved by Fritzing 0.9.2b)
circuit board: 6.5cm x 5.65cm
perfboards: 1

parts:
  R1 = Resistor [tolerance=±5% resistance=10k package=THT]
  R2 = Resistor [tolerance=±5% resistance=1k package=THT]
  Q1 = NPN-Transistor [package="TO92 [THT]"]
  C1 = Electrolytic Capacitor [capacitance=1µF voltage=50V package="100 mil [THT, electrolytic]"]
  Photoresistor = double row male pin header, 2 pins [form="♂ (male)"]
  Powerswitch = male pin header, 2 pins [form="♂ (male)"]
  LED = male pin header, 2 pins [form="♂ (male)"]
  Servo = male pin header, 3 pins [form="♂ (male)"]
  Raspberry_Pi1 = Raspberry Pi 2

nets:
  N1: R1.Pin_0, Q1.E, Servo.pin1, Raspberry_Pi1.GND
  N2: R1.Pin_1, R2.Pin_1, Powerswitch.pin1
  N3: R2.Pin_0, Raspberry_Pi1.GPIO17
  N4: Q1.B, Raspberry_Pi1.GPIO22
  N5: Q1.C, LED.pin2
  N6: C1.+, Photoresistor.pin2, Raspberry_Pi1.GPIO14
  3V3: Photoresistor.pin1, Powerswitch.pin2, Raspberry_Pi1.3v3, Raspberry_Pi1.3V3
  N7: LED.pin1, Servo.pin3, Raspberry_Pi1.5V
  N8: Servo.pin2, Raspberry_Pi1.GPIO18

notes:
  GPIO
  Switch
  PR
  LED
  Servo
  1kOhm
  10kOhm
  1uF 50V
  BC547B
  + drillhole
