# Fritzing sketch letterbox_board (saved by Fritzing 0.9.0b)
perfboards: 1

parts:
  CONN1 = USB connector [package=THT]
  R1 = Resistor [tolerance=±5% resistance=10k package=THT]
  R2 = Resistor [tolerance=±5% resistance=1k package=THT]
  Q1 = NPN-Transistor [package="TO92 [THT]"]
  C1 = Electrolytic Capacitor [capacitance=1µF voltage=50V package="100 mil [THT, electrolytic]"]
  J4 = double row male pin header, 2 pins [form="♂ (male)"]
  J3 = male pin header, 2 pins [form="♂ (male)"]
  J6 = male pin header, 2 pins [form="♂ (male)"]
  J5 = male pin header, 3 pins [form="♂ (male)"]
  J2 = female pin header, 13 pins [form="♀ (female)"]
  J1 = female pin header, 13 pins [form="♀ (female)"]

nets:
  N1: CONN1.5V, J6.pin1
  N2: CONN1.GND, CONN1.chassis5, CONN1.chassis6, J2.pin13
  N3: R1.Pin_0, J5.pin1
  N4: R1.Pin_1, R2.Pin_0, J4.pin1
  N5: R2.Pin_1, J2.pin6
  N6: Q1.B, J2.pin8
  N7: Q1.C, J6.pin2
  N8: C1.-, J2.pin5
  N9: C1.+, J3.pin1, J2.pin4
  N10: J4.pin2, J3.pin2, J2.pin1
  N11: J5.pin2, J1.pin6

notes:
  GPIO
  PW SW
  PR
  LED
  Servo
  1kOhm
  10kOhm
  1uF 50V
  BC547B
  + drillhole
